# Fritzing sketch schema_esempio_lezione (saved by Fritzing 0.9.3b)

parts:
  Raspberry_Pi_1 = Raspberry Pi 3 [part_number=RPI-3-V1.2]
  LED1 = LED - 5mm [color="Red (633nm)" package="5 mm [THT]"]
  LED2 = LED - 5mm [color="Green (565nm)" package="5 mm [THT]"]
  LED3 = LED - 5mm [color="Yellow (585nm)" package="5 mm [THT]"]
  R1 = Resistor [tolerance=±5% resistance=100 package=THT]
  R2 = Resistor [tolerance=±5% resistance=100 package=THT]
  R3 = Resistor [tolerance=±5% resistance=100 package=THT]
  S1 = Pushbutton [package="[THT]"]
  R4 = Resistor [tolerance=±5% resistance=15k package=THT]
  C1 = Ceramic Capacitor [capacitance=100nF package="100 mil [THT, multilayer]"]
  R5 = Resistor [tolerance=±5% resistance=1.2k package=THT]

nets:
  3V3: Raspberry_Pi_1.3v3, Raspberry_Pi_1.3V3, R4.Pin_1
  N1: Raspberry_Pi_1.GIPO22, S1.Pin_1, S1.Pin_2, R4.Pin_0, C1.1
  N2: Raspberry_Pi_1.GIPO5, R3.Pin_1
  N3: Raspberry_Pi_1.GIPO6, R1.Pin_1
  N4: Raspberry_Pi_1.GIPO26, R2.Pin_1
  N5: Raspberry_Pi_1.GND, LED1.cathode, LED2.cathode, LED3.cathode, S1.Pin_3, S1.Pin_4, R5.Pin_0
  N6: LED1.anode, R3.Pin_0
  N7: LED2.anode, R1.Pin_0
  N8: LED3.anode, R2.Pin_0
  N9: C1.0, R5.Pin_1
